// Logisim project ESF.circ as structural Verilog: 13 circuits, main circuit main
module main (
  output halt,
  output [31:0] out_2,
  output [31:0] out_3
);

  wire and_1_out, clock_1_out, clock_2_out, comparator_1_eq, comparator_2_eq, comparator_3_eq, not_1_out,
       or_1_out, register_7_q;
  wire [2:0] counter_2_q;
  wire [4:0] adder_1_out, counter_1_q;
  wire [15:0] key_schedule_1_out_7, multiplexer_5_out, register_5_q;
  wire [31:0] key_schedule_1_out_5, key_schedule_1_out_6, multiplexer_1_out, multiplexer_3_out,
       multiplexer_4_out, ram_1_data, ram_2_data, ram_3_data, ram_4_data, ram_5_data, register_1_q,
       register_2_q, register_3_q, register_4_q, round_function_1_out_3, shifter_1_out;

  Register #(.width(32)) register_1 (.D(out_2), .Q(register_1_q), .clk(or_1_out));  // open: en, clr
  Multiplexer #(.width(32)) multiplexer_1 (
    .in0(register_2_q), .in1(ram_1_data), .out(multiplexer_1_out), .sel(comparator_1_eq));  // open: en
  Register #(.width(32)) register_2 (.D(out_3), .Q(register_2_q), .clk(or_1_out));  // open: en, clr
  RAM #(.addrWidth(3), .dataWidth(32)) ram_1 (.addr(3'b000), .data(ram_1_data));  // open: sel, clk, ld, clr
  Shifter #(.width(32), .shift("rl")) shifter_1 (.in(multiplexer_1_out), .\dist (5'b00111), .out(shifter_1_out));
  // Probe on out_2
  Multiplexer #(.width(32)) multiplexer_2 (
    .in0(register_1_q), .in1(ram_2_data), .out(out_3), .sel(comparator_1_eq));  // open: en
  assign out_2 = shifter_1_out ^ round_function_1_out_3;  // XOR_Gate xor_1, 32 bits wide
  RAM #(.addrWidth(3), .dataWidth(32)) ram_2 (.addr(3'b001), .data(ram_2_data));  // open: sel, clk, ld, clr
  // Probe on out_3
  Multiplexer #(.width(32)) multiplexer_3 (
    .in0(register_3_q), .in1(ram_3_data), .out(multiplexer_3_out), .sel(comparator_1_eq));  // open: en
  round_function round_function_1 (.in_1(multiplexer_3_out), .in_2(out_3), .out_3(round_function_1_out_3));
  RAM #(.addrWidth(3), .dataWidth(32)) ram_3 (.addr(3'b010), .data(ram_3_data));  // open: sel, clk, ld, clr
  Register #(.width(32)) register_3 (.D(key_schedule_1_out_5), .Q(register_3_q), .clk(or_1_out));  // open: en, clr
  Multiplexer #(.width(32)) multiplexer_4 (
    .in0(register_4_q), .in1(ram_4_data), .out(multiplexer_4_out), .sel(comparator_1_eq));  // open: en
  key_schedule key_schedule_1 (
    .in_1(multiplexer_3_out), .in_2(multiplexer_4_out), .in_3(adder_1_out), .in_4(multiplexer_5_out),
    .out_5(key_schedule_1_out_5), .out_6(key_schedule_1_out_6), .out_7(key_schedule_1_out_7));
  Register #(.width(32)) register_4 (.D(key_schedule_1_out_6), .Q(register_4_q), .clk(or_1_out));  // open: en, clr
  RAM #(.addrWidth(3), .dataWidth(32)) ram_4 (.addr(3'b011), .data(ram_4_data));  // open: sel, clk, ld, clr
  Multiplexer #(.width(16)) multiplexer_5 (
    .in0(register_5_q), .in1(ram_5_data[15:0]), .out(multiplexer_5_out), .sel(comparator_1_eq));  // open: en
  Register #(.width(16)) register_5 (.D(key_schedule_1_out_7), .Q(register_5_q), .clk(or_1_out));  // open: en, clr
  Comparator #(.width(5), .mode("unsigned")) comparator_1 (
    .a(counter_1_q), .b({5{1'b0}}), .eq(comparator_1_eq));  // open: gt, lt
  not not_1 (not_1_out, or_1_out);
  Clock clock_1 (.out(clock_1_out));
  and and_1 (and_1_out, clock_1_out, comparator_2_eq);
  RAM #(.addrWidth(3), .dataWidth(32)) ram_5 (.addr(3'b100), .data(ram_5_data));  // open: sel, clk, ld, clr
  Counter #(.width(5), .max('h1f), .ongoal("stay")) counter_1 (
    .D({5{1'b0}}), .count(1'b1), .Q(counter_1_q), .clk(not_1_out));  // open: load, carry, clr
  or or_1 (or_1_out, register_7_q, and_1_out);
  Counter #(.width(3), .max('h7), .ongoal("stay")) counter_2 (
    .count(1'b1), .Q(counter_2_q), .clk(clock_2_out));  // open: load, D, carry, clr
  Clock clock_2 (.out(clock_2_out));
  Comparator #(.width(3), .mode("unsigned")) comparator_2 (
    .a(counter_2_q), .b(3'b111), .eq(comparator_2_eq));  // open: gt, lt
  Register #(.width(1)) register_6 (.D(comparator_3_eq), .Q(halt), .clk(or_1_out));  // open: en, clr
  Comparator #(.width(5), .mode("unsigned")) comparator_3 (
    .a(counter_1_q), .b(5'b11110), .eq(comparator_3_eq));  // open: gt, lt
  Register #(.width(1)) register_7 (.D(comparator_3_eq), .Q(register_7_q), .clk(and_1_out));  // open: en, clr
  Adder #(.width(5)) adder_1 (.a(counter_1_q), .b(5'b00001), .out(adder_1_out));  // open: cin, cout
endmodule

module S0 (
  input  [3:0] in_1,
  output [3:0] out_2
);

  Multiplexer #(.select(4), .width(4)) multiplexer_1 (
    .in0(4'b0011), .in1(4'b1000), .in2(4'b1111), .in3(4'b0001), .in4(4'b1010), .in5(4'b0110), .in6(4'b0101),
    .in7(4'b1011), .in8(4'b1110), .in9(4'b1101), .in10(4'b0100), .in11(4'b0010), .in12(4'b0111),
    .in13(4'b0000), .in14(4'b1001), .in15(4'b1100), .out(out_2), .sel(in_1));  // open: en
endmodule

module S1 (
  input  [3:0] in_1,
  output [3:0] out_2
);

  Multiplexer #(.select(4), .width(4)) multiplexer_1 (
    .in0(4'b1111), .in1(4'b1100), .in2(4'b0010), .in3(4'b0111), .in4(4'b1001), .in5(4'b0000), .in6(4'b0101),
    .in7(4'b1010), .in8(4'b0001), .in9(4'b1011), .in10(4'b1110), .in11(4'b1000), .in12(4'b0110),
    .in13(4'b1101), .in14(4'b0011), .in15(4'b0100), .out(out_2), .sel(in_1));  // open: en
endmodule

module S2 (
  input  [3:0] in_1,
  output [3:0] out_2
);

  Multiplexer #(.select(4), .width(4)) multiplexer_1 (
    .in0(4'b1000), .in1(4'b0110), .in2(4'b0111), .in3(4'b1001), .in4(4'b0011), .in5(4'b1100), .in6(4'b1010),
    .in7(4'b1111), .in8(4'b1101), .in9(4'b0001), .in10(4'b1110), .in11(4'b0100), .in12(4'b0000),
    .in13(4'b1011), .in14(4'b0101), .in15(4'b0010), .out(out_2), .sel(in_1));  // open: en
endmodule

module S3 (
  input  [3:0] in_1,
  output [3:0] out_2
);

  Multiplexer #(.select(4), .width(4)) multiplexer_1 (
    .in0(4'b0000), .in1(4'b1111), .in2(4'b1011), .in3(4'b1000), .in4(4'b1100), .in5(4'b1001), .in6(4'b0110),
    .in7(4'b0011), .in8(4'b1101), .in9(4'b0001), .in10(4'b0010), .in11(4'b0100), .in12(4'b1010),
    .in13(4'b0111), .in14(4'b0101), .in15(4'b1110), .out(out_2), .sel(in_1));  // open: en
endmodule

module S4 (
  input  [3:0] in_1,
  output [3:0] out_2
);

  Multiplexer #(.select(4), .width(4)) multiplexer_1 (
    .in0(4'b0001), .in1(4'b1111), .in2(4'b1000), .in3(4'b0011), .in4(4'b1100), .in5(4'b0000), .in6(4'b1011),
    .in7(4'b0110), .in8(4'b0010), .in9(4'b0101), .in10(4'b0100), .in11(4'b1010), .in12(4'b1001),
    .in13(4'b1110), .in14(4'b0111), .in15(4'b1101), .out(out_2), .sel(in_1));  // open: en
endmodule

module S5 (
  input  [3:0] in_1,
  output [3:0] out_2
);

  Multiplexer #(.select(4), .width(4)) multiplexer_1 (
    .in0(4'b1111), .in1(4'b0101), .in2(4'b0010), .in3(4'b1011), .in4(4'b0100), .in5(4'b1010), .in6(4'b1001),
    .in7(4'b1100), .in8(4'b0000), .in9(4'b0011), .in10(4'b1110), .in11(4'b1000), .in12(4'b1101),
    .in13(4'b0110), .in14(4'b0111), .in15(4'b0001), .out(out_2), .sel(in_1));  // open: en
endmodule

module S6 (
  input  [3:0] in_1,
  output [3:0] out_2
);

  Multiplexer #(.select(4), .width(4)) multiplexer_1 (
    .in0(4'b0111), .in1(4'b0010), .in2(4'b1100), .in3(4'b0101), .in4(4'b1000), .in5(4'b0100), .in6(4'b0110),
    .in7(4'b1011), .in8(4'b1110), .in9(4'b1001), .in10(4'b0001), .in11(4'b1111), .in12(4'b1101),
    .in13(4'b0011), .in14(4'b1010), .in15(4'b0000), .out(out_2), .sel(in_1));  // open: en
endmodule

module S7 (
  input  [3:0] in_1,
  output [3:0] out_2
);

  Multiplexer #(.select(4), .width(4)) multiplexer_1 (
    .in0(4'b0001), .in1(4'b1101), .in2(4'b1111), .in3(4'b0000), .in4(4'b1110), .in5(4'b1000), .in6(4'b0010),
    .in7(4'b1011), .in8(4'b0111), .in9(4'b0100), .in10(4'b1100), .in11(4'b1010), .in12(4'b1001),
    .in13(4'b0011), .in14(4'b0101), .in15(4'b0110), .out(out_2), .sel(in_1));  // open: en
endmodule

module permutation (
  input  [31:0] in_1,
  output [31:0] out_2
);


  assign out_2 = {in_1[31], in_1[27], in_1[23], in_1[19], in_1[15], in_1[11], in_1[7], in_1[3], in_1[30], in_1[26], in_1[22], in_1[18], in_1[14], in_1[10], in_1[6], in_1[2], in_1[29], in_1[25], in_1[21], in_1[17], in_1[13], in_1[9], in_1[5], in_1[1], in_1[28], in_1[24], in_1[20], in_1[16], in_1[12], in_1[8], in_1[4], in_1[0]};
endmodule

module key_schedule (
  input  [31:0] in_1,
  input  [31:0] in_2,
  input  [4:0] in_3,
  input  [15:0] in_4,
  output [31:0] out_5,
  output [31:0] out_6,
  output [15:0] out_7
);

  S0 s0_1 (.in_1(in_1[14:11]), .out_2(out_5[27:24]));
  S0 s0_2 (.in_1(in_1[18:15]), .out_2(out_5[31:28]));
  assign out_6[31:27] = in_2[18:14] ^ in_3;  // XOR_Gate xor_1, 5 bits wide

  assign out_5[23:0] = {in_1[10:0], in_2[31:19]};
  assign out_6[26:0] = {in_2[13:0], in_4[15:3]};
  assign out_7 = {in_4[2:0], in_1[31:19]};
endmodule

module round_function (
  input  [31:0] in_1,
  input  [31:0] in_2,
  output [31:0] out_3
);

  wire [3:0] s0_1_out_2, s1_1_out_2, s2_1_out_2, s3_1_out_2, s4_1_out_2, s5_1_out_2, s6_1_out_2, s7_1_out_2;
  wire [31:0] xor_1_out;

  assign xor_1_out = in_1 ^ in_2;  // XOR_Gate xor_1, 32 bits wide
  S0 s0_1 (.in_1(xor_1_out[3:0]), .out_2(s0_1_out_2));
  S1 s1_1 (.in_1(xor_1_out[7:4]), .out_2(s1_1_out_2));
  S2 s2_1 (.in_1(xor_1_out[11:8]), .out_2(s2_1_out_2));
  S3 s3_1 (.in_1(xor_1_out[15:12]), .out_2(s3_1_out_2));
  S4 s4_1 (.in_1(xor_1_out[19:16]), .out_2(s4_1_out_2));
  S5 s5_1 (.in_1(xor_1_out[23:20]), .out_2(s5_1_out_2));
  S6 s6_1 (.in_1(xor_1_out[27:24]), .out_2(s6_1_out_2));
  S7 s7_1 (.in_1(xor_1_out[31:28]), .out_2(s7_1_out_2));
  permutation permutation_1 (
    .in_1({s7_1_out_2, s6_1_out_2, s5_1_out_2, s4_1_out_2, s3_1_out_2, s2_1_out_2, s1_1_out_2, s0_1_out_2}),
    .out_2(out_3));
endmodule

module rotate (
  input  [31:0] in_1,
  output [31:0] out_2
);

  Shifter #(.width(32), .shift("rl")) shifter_1 (.in(in_1), .\dist (5'b00111), .out(out_2));
endmodule
