// Logisim project PRESENT.circ as structural Verilog: 7 circuits, main circuit main
module main (
  output [4:0] out_1,
  output [31:0] out_2,
  output [31:0] out_3
);

  wire clock_1_out, comparator_1_eq, comparator_2_eq, not_1_out, or_1_out, register_6_q;
  wire [4:0] adder_1_out;
  wire [15:0] key_schedule_1_out_5, multiplexer_5_out, register_3_q;
  wire [31:0] add_round_key_1_out_5, add_round_key_1_out_6, key_schedule_1_out_6, key_schedule_1_out_7,
       multiplexer_1_out, multiplexer_2_out, multiplexer_3_out, multiplexer_4_out, p_layer_1_out_3,
       p_layer_1_out_4, register_1_q, register_2_q, register_4_q, register_5_q, s_layer_1_out_3,
       s_layer_1_out_4;

  Register #(.width(32)) register_1 (.D(out_3), .Q(register_1_q), .clk(or_1_out));  // open: en, clr
  Register #(.width(32)) register_2 (.D(out_2), .Q(register_2_q), .clk(or_1_out));  // open: en, clr
  add_round_key add_round_key_1 (
    .in_1({32{1'b1}}), .in_2({32{1'b0}}), .out_5(add_round_key_1_out_5), .in_3({32{1'b1}}),
    .in_4({32{1'b0}}), .out_6(add_round_key_1_out_6));
  Multiplexer #(.width(32)) multiplexer_1 (
    .in0(register_2_q), .in1(add_round_key_1_out_6), .out(multiplexer_1_out), .sel(comparator_1_eq));  // open: en
  Multiplexer #(.width(32)) multiplexer_2 (
    .in0(register_1_q), .in1(add_round_key_1_out_5), .out(multiplexer_2_out), .sel(comparator_1_eq));  // open: en
  s_layer s_layer_1 (
    .in_1(multiplexer_2_out), .in_2(multiplexer_1_out), .out_3(s_layer_1_out_3), .out_4(s_layer_1_out_4));
  p_layer p_layer_1 (.in_1(s_layer_1_out_3), .in_2(s_layer_1_out_4), .out_3(p_layer_1_out_3), .out_4(p_layer_1_out_4));
  add_round_key add_round_key_2 (
    .in_1(p_layer_1_out_3), .in_2(key_schedule_1_out_6), .out_5(out_3), .in_3(p_layer_1_out_4),
    .in_4(key_schedule_1_out_7), .out_6(out_2));
  Multiplexer #(.width(32)) multiplexer_3 (
    .in0(register_5_q), .in1({32{1'b0}}), .out(multiplexer_3_out), .sel(comparator_1_eq));  // open: en
  key_schedule key_schedule_1 (
    .in_1(multiplexer_3_out), .in_2(adder_1_out), .in_3(multiplexer_4_out), .in_4(multiplexer_5_out),
    .out_5(key_schedule_1_out_5), .out_6(key_schedule_1_out_6), .out_7(key_schedule_1_out_7));
  Multiplexer #(.width(32)) multiplexer_4 (
    .in0(register_4_q), .in1({32{1'b0}}), .out(multiplexer_4_out), .sel(comparator_1_eq));  // open: en
  Multiplexer #(.width(16)) multiplexer_5 (
    .in0(register_3_q), .in1({16{1'b0}}), .out(multiplexer_5_out), .sel(comparator_1_eq));  // open: en
  Register #(.width(16)) register_3 (.D(key_schedule_1_out_5), .Q(register_3_q), .clk(or_1_out));  // open: en, clr
  Register #(.width(32)) register_4 (.D(key_schedule_1_out_7), .Q(register_4_q), .clk(or_1_out));  // open: en, clr
  Comparator #(.width(5), .mode("unsigned")) comparator_1 (
    .a(out_1), .b({5{1'b0}}), .eq(comparator_1_eq));  // open: gt, lt
  Register #(.width(32)) register_5 (.D(key_schedule_1_out_6), .Q(register_5_q), .clk(or_1_out));  // open: en, clr
  not not_1 (not_1_out, or_1_out);
  Clock clock_1 (.out(clock_1_out));
  Counter #(.width(5), .max('h1f), .ongoal("stay")) counter_1 (
    .D({5{1'b0}}), .count(1'b1), .Q(out_1), .clk(not_1_out));  // open: load, carry, clr
  or or_1 (or_1_out, register_6_q, clock_1_out);
  Comparator #(.width(5), .mode("unsigned")) comparator_2 (
    .a(out_1), .b(5'b11110), .eq(comparator_2_eq));  // open: gt, lt
  Register #(.width(1)) register_6 (.D(comparator_2_eq), .Q(register_6_q), .clk(clock_1_out));  // open: en, clr
  Adder #(.width(5)) adder_1 (.a(out_1), .b(5'b00001), .out(adder_1_out));  // open: cin, cout
endmodule

module s_box (
  input  [3:0] in_1,
  output [3:0] out_2
);

  Multiplexer #(.select(4), .width(4)) multiplexer_1 (
    .in0(4'b1100), .in1(4'b0101), .in2(4'b0110), .in3(4'b1011), .in4(4'b1001), .in5(4'b0000), .in6(4'b1010),
    .in7(4'b1101), .in8(4'b0011), .in9(4'b1110), .in10(4'b1111), .in11(4'b1000), .in12(4'b0100),
    .in13(4'b0111), .in14(4'b0001), .in15(4'b0010), .out(out_2), .sel(in_1));  // open: en
endmodule

module p_layer (
  input  [31:0] in_1,
  input  [31:0] in_2,
  output [31:0] out_3,
  output [31:0] out_4
);


  assign out_3 = {in_1[31], in_1[27], in_1[23], in_1[19], in_1[15], in_1[11], in_1[7], in_1[3], in_2[31], in_2[27], in_2[23], in_2[19], in_2[15], in_2[11], in_2[7], in_2[3], in_1[30], in_1[26], in_1[22], in_1[18], in_1[14], in_1[10], in_1[6], in_1[2], in_2[30], in_2[26], in_2[22], in_2[18], in_2[14], in_2[10], in_2[6], in_2[2]};
  assign out_4 = {in_1[29], in_1[25], in_1[21], in_1[17], in_1[13], in_1[9], in_1[5], in_1[1], in_2[29], in_2[25], in_2[21], in_2[17], in_2[13], in_2[9], in_2[5], in_2[1], in_1[28], in_1[24], in_1[20], in_1[16], in_1[12], in_1[8], in_1[4], in_1[0], in_2[28], in_2[24], in_2[20], in_2[16], in_2[12], in_2[8], in_2[4], in_2[0]};
endmodule

module key_schedule (
  input  [31:0] in_1,
  input  [4:0] in_2,
  input  [31:0] in_3,
  input  [15:0] in_4,
  output [15:0] out_5,
  output [31:0] out_6,
  output [31:0] out_7
);

  s_box s_box_1 (.in_1({in_3[2:0], in_4[15]}), .out_2(out_6[31:28]));
  assign {out_7[3:0], out_5[15]} = in_3[22:18] ^ in_2;  // XOR_Gate xor_1, 5 bits wide

  assign out_5[14:0] = in_3[17:3];
  assign out_6[27:0] = {in_4[14:0], in_1[31:19]};
  assign out_7[31:4] = {in_1[18:0], in_3[31:23]};
endmodule

module s_layer (
  input  [31:0] in_1,
  input  [31:0] in_2,
  output [31:0] out_3,
  output [31:0] out_4
);

  s_box s_box_1 (.in_1(in_1[3:0]), .out_2(out_3[3:0]));
  s_box s_box_2 (.in_1(in_1[7:4]), .out_2(out_3[7:4]));
  s_box s_box_3 (.in_1(in_1[11:8]), .out_2(out_3[11:8]));
  s_box s_box_4 (.in_1(in_1[15:12]), .out_2(out_3[15:12]));
  s_box s_box_5 (.in_1(in_1[19:16]), .out_2(out_3[19:16]));
  s_box s_box_6 (.in_1(in_1[23:20]), .out_2(out_3[23:20]));
  s_box s_box_7 (.in_1(in_1[27:24]), .out_2(out_3[27:24]));
  s_box s_box_8 (.in_1(in_1[31:28]), .out_2(out_3[31:28]));
  s_box s_box_9 (.in_1(in_2[3:0]), .out_2(out_4[3:0]));
  s_box s_box_10 (.in_1(in_2[7:4]), .out_2(out_4[7:4]));
  s_box s_box_11 (.in_1(in_2[11:8]), .out_2(out_4[11:8]));
  s_box s_box_12 (.in_1(in_2[15:12]), .out_2(out_4[15:12]));
  s_box s_box_13 (.in_1(in_2[19:16]), .out_2(out_4[19:16]));
  s_box s_box_14 (.in_1(in_2[23:20]), .out_2(out_4[23:20]));
  s_box s_box_15 (.in_1(in_2[27:24]), .out_2(out_4[27:24]));
  s_box s_box_16 (.in_1(in_2[31:28]), .out_2(out_4[31:28]));
endmodule

module add_round_key (
  input  [31:0] in_1,
  input  [31:0] in_2,
  input  [31:0] in_3,
  input  [31:0] in_4,
  output [31:0] out_5,
  output [31:0] out_6
);

  assign out_5 = in_1 ^ in_2;  // XOR_Gate xor_1, 32 bits wide
  assign out_6 = in_3 ^ in_4;  // XOR_Gate xor_2, 32 bits wide
endmodule

module clock (
  output [4:0] out_1,
  output [4:0] out_2
);

  wire clock_1_out, clock_2_out, comparator_1_eq, or_1_out, register_1_q;

  Counter #(.width(5), .max('h1f), .ongoal("stay")) counter_1 (
    .load(1'b0), .D({5{1'b0}}), .count(1'b1), .Q(out_2), .clk(clock_1_out));  // open: carry, clr
  Clock clock_1 (.out(clock_1_out));
  Clock clock_2 (.out(clock_2_out));
  Counter #(.width(5), .max('h1f), .ongoal("stay")) counter_2 (
    .D({5{1'b0}}), .count(1'b1), .Q(out_1), .clk(or_1_out));  // open: load, carry, clr
  or or_1 (or_1_out, register_1_q, clock_2_out);
  Comparator #(.width(5), .mode("unsigned")) comparator_1 (
    .a(out_1), .b({5{1'b1}}), .eq(comparator_1_eq));  // open: gt, lt
  Register #(.width(1)) register_1 (.D(comparator_1_eq), .Q(register_1_q), .clk(clock_2_out));  // open: en, clr
endmodule
